# Fritzing sketch circuit (saved by Fritzing 0.9.3b)
breadboards: 1
perfboards: 1

parts:
  Composant1 = 12 NeoPixel Ring [part_number=1643]
  Composant2 = 16 NeoPixel Ring [part_number=1463]
  U1 = attiny85 [package=dip]
  VCC1 = 4 x AAA Battery Mount
  C1 = Capacitor Polarized [package=cpol-radial-1000uf-63v]
  R1 = Resistor [tolerance=±5% resistance=220 package=THT]
  IR1 = TSOP312.., 314.. [package=THT]

nets:
  N1: Composant1.IN, R1.Pin_0
  N2: Composant1.OUT, Composant2.IN
  VDD: Composant1.VDD, Composant2.VDD, U1.Pin_8, VCC1.+, C1.+, IR1.Vs
  GND: Composant1.GND, Composant2.GND, U1.Pin_4, VCC1.-, C1.-, IR1.GND
  N3: U1.Pin_3, IR1.Data
  N4: U1.Pin_6, R1.Pin_1

custom parts:
  12 NeoPixel Ring: 12 ultra bright smart LED NeoPixels are arranged in a circle with 1.5" (37mm) outer diameter. The rings are 'chainable' - connect the output pin of one to the input pin of another. Use only one microcontroller pin to control as many as you can chain together! Each LED is addressable as the driver chip is inside the LED. Each one has ~18mA constant current drive so the color will be very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
  16 NeoPixel Ring: 16 ultra bright smart LED NeoPixels are arranged in a circle with 1.75" (44.5mm) outer diameter. The rings are 'chainable' - connect the output pin of one to the input pin of another. Use only one microcontroller pin to control as many as you can chain together! Each LED is addressable as the driver chip is inside the LED. Each one has ~18mA constant current drive so the color will be very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
